// Logisim project Assignment 1 Part 2.circ as structural Verilog: 1 circuit, main circuit main
module main (
  input  J1,
  input  J0,
  input  B1,
  input  B0,
  output out_5,
  output out_6
);

  wire and_1_out, and_2_out, and_3_out, and_4_out, not_1_out, not_2_out, not_3_out, not_4_out;

  not not_1 (not_1_out, J1);
  not not_2 (not_2_out, J0);
  not not_3 (not_3_out, B1);
  not not_4 (not_4_out, B0);
  and and_1 (and_1_out, not_2_out, B1, B0);
  and and_2 (and_2_out, not_1_out, B1, B0);
  and and_3 (and_3_out, J0, J1, not_3_out);
  and and_4 (and_4_out, J0, J1, not_4_out);
  or or_1 (out_5, and_1_out, and_2_out);
  or or_2 (out_6, and_3_out, and_4_out);
endmodule
